// Logisim project ProjetodearquiteturaFalcon8.circ as structural Verilog: 7 circuits, main circuit main
module main (
  input  RST
);

  wire ALUSrc, ALUzero, CLK, MenRead, MenToReg, MenWrite, or_1_out, PCSrc, RegWrite, Tipo_B_GERAL;
  wire [2:0] ALUop, FUNCT, ImmSel, rdDecode, rs1, rs2, rs2Decode;
  wire [3:0] OPCODE;
  wire [5:0] B_IMM, I_IMM, S_IMM;
  wire [7:0] alu_result, controlled_buffer_1_out, imediato, multiplexer_2_out, ram_data_out, rd1, rd2,
       writeback_data;
  wire [8:0] J_IMM;
  wire [15:0] instructionfetch_1_instrucao;

  Clock u_CLK (.out(CLK));
  // Probe on B_IMM
  // Probe on J_IMM
  // Probe on ImmSel
  // Probe on imediato
  // Probe on imediato
  ImmGen immgen_1 (
    .ImmSel(ImmSel), .i_imm(I_IMM), .S_imm(S_IMM), .B_imm(B_IMM), .J_imm(J_IMM), .imediato(imediato));  // open: in_5
  InstructionFetch instructionfetch_1 (
    .imediato(imediato), .PCSrc(PCSrc), .CLK(CLK), .RST(RST), .instrucao(instructionfetch_1_instrucao));
  // Probe on instructionfetch_1_instrucao
  // Probe on rdDecode
  InstructionDecode instructiondecode_1 (
    .instrucao(instructionfetch_1_instrucao), .OPCODE(OPCODE), .rd(rdDecode), .rs1(rs1), .rs2(rs2Decode),
    .FUNCT(FUNCT), .I_MM(I_IMM), .S_IMM(S_IMM), .B_IMM(B_IMM), .J_IMM(J_IMM));
  // Probe on rs1
  // Probe on OPCODE
  // Probe on ImmSel
  UC uc_1 (
    .opcode(OPCODE), .Funct3(FUNCT), .CLK(CLK), .ALUzero(ALUzero), .ImmSel(ImmSel), .ALUOp(ALUop),
    .ALUSrc(ALUSrc), .Tipo_B_GERAL(Tipo_B_GERAL), .MenRead(MenRead), .MenToReg(MenToReg),
    .MenWrite(MenWrite), .RegWrite(RegWrite), .PCSrc(PCSrc));
  Multiplexer #(.width(3)) multiplexer_1 (.in0(rs2Decode), .in1(rdDecode), .out(rs2), .sel(or_1_out));
  or or_1 (or_1_out, MenWrite, Tipo_B_GERAL);
  // Probe on ALUop
  // Probe on rd1
  BR br_1 (
    .rs1(rs1), .rs2(rs2), .rd(rdDecode), .Data(writeback_data), .RegWrite(RegWrite), .CLK(CLK), .RST(RST),
    .rd1(rd1), .rd2(rd2));
  // Probe on imediato
  // Probe on rd2
  // Probe on multiplexer_2_out
  Multiplexer #(.width(8)) multiplexer_2 (.in0(rd2), .in1(imediato), .out(multiplexer_2_out), .sel(ALUSrc));
  // Probe on ALUSrc
  // Probe on rd1
  // Probe on writeback_data
  Multiplexer #(.width(8)) multiplexer_3 (.in0(alu_result), .in1(ram_data_out), .out(writeback_data), .sel(MenToReg));
  // Probe on ALUop
  // Probe on rd2
  // Probe on alu_result
  assign controlled_buffer_1_out = MenWrite ? rd2 : 8'bz;  // Controlled_Buffer controlled_buffer_1
  ULA ula_1 (.src1(rd1), .src2(multiplexer_2_out), .ALUOperation(ALUop), .ALUzero(ALUzero), .result(alu_result));
  // Probe on alu_result
  RAM #(.asyncread("true"), .trigger("falling")) ram_1 (
    .addr(alu_result), .we(MenWrite), .oe(MenRead), .clk(CLK), .din(controlled_buffer_1_out),
    .dout(ram_data_out));
  // Probe on ram_data_out
endmodule

module InstructionDecode (
  input  [15:0] instrucao,
  output [3:0] OPCODE,
  output [2:0] rd,
  output [2:0] rs1,
  output [2:0] rs2,
  output [2:0] FUNCT,
  output [5:0] I_MM,
  output [5:0] S_IMM,
  output [5:0] B_IMM,
  output [8:0] J_IMM
);

  // Probe on instrucao[5:3]
  // Probe on nothing
  // Probe on instrucao[8:6]
  // Probe on instrucao[11:9]
  // Probe on instrucao[15:12]
  // Probe on instrucao[2:0]
  // Probe on instrucao[5:0]

  assign B_IMM = instrucao[5:0];
  assign FUNCT = instrucao[2:0];
  assign I_MM = instrucao[5:0];
  assign J_IMM = {instrucao[5:3], instrucao[8:6], instrucao[2:0]};
  assign OPCODE = instrucao[15:12];
  assign rd = instrucao[11:9];
  assign rs1 = instrucao[8:6];
  assign rs2 = instrucao[5:3];
  assign S_IMM = instrucao[5:0];

  // Other names for the same wires on the sheet: I_IMM[5:0] = instrucao[5:0]; IMM6[5:0] = instrucao[5:0]

  // Notes on the sheet:
  //   0-2 FUNCT
  //   3-5 RS2
  //   8-6 RS1
  //   11-9 RD
  //   15-12 OPCODE
endmodule

module InstructionFetch (
  input  [7:0] imediato,
  input  PCSrc,
  input  CLK,
  input  RST,
  output [15:0] instrucao
);

  wire [7:0] nextPC, PC_branch, PC_plus2, PC_q;

  // Probe on imediato
  Register PC (.D(nextPC), .en(1'b1), .clk(CLK), .Q(PC_q), .clr(RST));
  // Probe on imediato
  Adder adder_1 (.a(PC_q), .b(imediato), .out(PC_branch));  // open: cin, cout
  Adder adder_2 (.a(8'h2), .b(PC_q), .out(PC_plus2));  // open: cin, cout
  // Probe on {PC_q[0], PC_q[7:1]}
  // Probe on PC_plus2
  ROM #(.dataWidth(16)) rom_1 (.addr({PC_q[0], PC_q[7:1]}), .data(instrucao));
  // Probe on instrucao
  // Probe on nextPC
  Multiplexer #(.width(8)) multiplexer_1 (.in0(PC_plus2), .in1(PC_branch), .out(nextPC), .sel(PCSrc));
  // Probe on PCSrc

  // Notes on the sheet:
  //   Memoria de Instrucoes
  //   contents of rom_1 (hex, n*v repeats v):
  //   0 2210 2412 654 5606 1e10 ff8 31c0 31c1 6010 2811 2a13 d64 4c07 1e10 ff8 1802 39c0 39c1 6006 1e10
  //   ff8 1801 39c0 39c1 6000
endmodule

module BR (
  input  [2:0] rs1,
  input  [2:0] rs2,
  input  [2:0] rd,
  input  [7:0] Data,
  input  RegWrite,
  input  CLK,
  input  RST,
  output [7:0] rd1,
  output [7:0] rd2
);

  wire WE_x1, WE_x2, WE_x3, WE_x4, WE_x5, WE_x6, WE_x7;
  wire [7:0] Q_x0, Q_x1, Q_x2, Q_x3, Q_x4, Q_x5, Q_x6, Q_x7;

  // Probe on rd
  // Probe on rs1
  // Probe on WE_x1
  Demultiplexer #(.select(3)) demultiplexer_1 (
    .out1(WE_x1), .out2(WE_x2), .out3(WE_x3), .out4(WE_x4), .out5(WE_x5), .out6(WE_x6), .out7(WE_x7),
    .in(RegWrite), .sel(rd));  // open: out0
  // Probe on RegWrite
  Register #(.trigger("falling")) R0 (.D({8{1'b0}}), .en(1'b0), .clk(CLK), .Q(Q_x0), .clr(RST));
  Register #(.trigger("falling")) R4 (.D(Data), .en(WE_x4), .clk(CLK), .Q(Q_x4), .clr(RST));
  Multiplexer #(.select(3), .width(8)) multiplexer_1 (
    .in0(Q_x0), .in1(Q_x1), .in2(Q_x2), .in3(Q_x3), .in4(Q_x4), .in5(Q_x5), .in6(Q_x6), .in7(Q_x7),
    .out(rd1), .sel(rs1));
  Register #(.trigger("falling")) R1 (.D(Data), .en(WE_x1), .clk(CLK), .Q(Q_x1), .clr(RST));
  Register #(.trigger("falling")) R5 (.D(Data), .en(WE_x5), .clk(CLK), .Q(Q_x5), .clr(RST));
  Multiplexer #(.select(3), .width(8)) multiplexer_2 (
    .in0(Q_x0), .in1(Q_x1), .in2(Q_x2), .in3(Q_x3), .in4(Q_x4), .in5(Q_x5), .in6(Q_x6), .in7(Q_x7),
    .out(rd2), .sel(rs2));
  Register #(.trigger("falling")) R2 (.D(Data), .en(WE_x2), .clk(CLK), .Q(Q_x2), .clr(RST));
  Register #(.trigger("falling")) R6 (.D(Data), .en(WE_x6), .clk(CLK), .Q(Q_x6), .clr(RST));
  Register #(.trigger("falling")) R3 (.D(Data), .en(WE_x3), .clk(CLK), .Q(Q_x3), .clr(RST));
  Register #(.trigger("falling")) R7 (.D(Data), .en(WE_x7), .clk(CLK), .Q(Q_x7), .clr(RST));

  // Other names for the same wires on the sheet: rw = RegWrite
endmodule

module ULA (
  input  [7:0] src1,
  input  [7:0] src2,
  input  [2:0] ALUOperation,
  output ALUzero,
  output [7:0] result
);

  wire comparator_1_lt;
  wire [7:0] add, and_logic, or_logic, sll_logic, slt_logic, sra_logic, srl_logic, sub, xor_logic;

  assign xor_logic = src1 ^ src2;  // XOR_Gate xor_1, 8 bits wide
  assign or_logic = src1 | src2;  // OR_Gate or_1, 8 bits wide
  assign and_logic = src1 & src2;  // AND_Gate and_1, 8 bits wide
  Adder adder_1 (.a(src1), .b(src2), .out(add));  // open: cin, cout
  Subtractor subtractor_1 (.a(src1), .b(src2), .out(sub));  // open: bin, bout
  Shifter shifter_1 (.in(src1), .\dist (src2[2:0]), .out(sll_logic));
  Shifter #(.shift("lr")) shifter_2 (.in(src1), .\dist (src2[2:0]), .out(srl_logic));
  Shifter #(.shift("ar")) shifter_3 (.in(src1), .\dist (src2[2:0]), .out(sra_logic));
  Comparator comparator_1 (.a(src1), .b(src2), .lt(comparator_1_lt));  // open: gt, eq
  assign slt_logic = {{7{1'b0}}, comparator_1_lt};  // Bit_Extender bit_extender_1
  // Probe on slt_logic
  Multiplexer #(.select(3), .width(8)) multiplexer_1 (
    .in0(add), .in1(sub), .in2(and_logic), .in3(or_logic), .in4(slt_logic), .in5(xor_logic), .in6(srl_logic),
    .in7(sll_logic), .out(result), .sel(ALUOperation));
  Comparator comparator_2 (.a({8{1'b0}}), .b(result), .eq(ALUzero));  // open: gt, lt
  // Probe on result

  // Other names for the same wires on the sheet: ALUOp[2:0] = ALUOperation; scr2[7:0] = src2; zero = ALUzero

  // Notes on the sheet:
  //   Operações: 000 = ADD 001 = SUB 010 = AND 011 = OR 100 = SLT
endmodule

module ImmGen (
  input  [2:0] ImmSel,
  input  [5:0] i_imm,
  input  [5:0] S_imm,
  input  [5:0] B_imm,
  input  [7:0] in_5,
  input  [8:0] J_imm,
  output [7:0] imediato
);

  wire [7:0] B_8b, I_8b, S_8b;

  // Probe on {J_imm[6:0], 1'b0}
  assign I_8b = {{2{i_imm[5]}}, i_imm};  // Bit_Extender bit_extender_1
  assign S_8b = {{2{1'b0}}, S_imm};  // Bit_Extender bit_extender_2
  assign B_8b = {{1{1'b0}}, {B_imm, 1'b0}};  // Bit_Extender bit_extender_3
  // Probe on B_8b
  // Probe on S_8b
  // Probe on I_8b
  Multiplexer #(.select(3), .width(8)) multiplexer_1 (
    .in0(I_8b), .in1(S_8b), .in2(B_8b), .in3(in_5), .in4({J_imm[6:0], 1'b0}), .out(imediato), .sel(ImmSel));  // open: in5, in6, in7

  // Other names for the same wires on the sheet: J_8b[7:1] = J_imm[6:0]; Imm[7:0] = imediato; U_8b[7:0] = in_5

  // Notes on the sheet:
  //   Instrucao tipo S
  //   Instrucao tipo I
  //   Instrucao tipo B
  //   Instrucao tipo u
  //   Instrucao tipo J
endmodule

module UC (
  input  [3:0] opcode,
  input  [2:0] Funct3,
  input  CLK,
  input  ALUzero,
  output [2:0] ImmSel,
  output [2:0] ALUOp,
  output ALUSrc,
  output Tipo_B_GERAL,
  output MenRead,
  output MenToReg,
  output MenWrite,
  output RegWrite,
  output PCSrc
);

  wire branch_cond, branch_taken, is_I, is_U, Tipo_B, Tipo_B_BNE, Tipo_I_AR, Tipo_U_LUI;
  wire [0:0] ALUOpSel;

  Decoder #(.select(4)) decoder_1 (
    .out0(ALUOpSel[0]), .out1(Tipo_I_AR), .out2(MenToReg), .out3(MenWrite), .out4(Tipo_B), .out5(Tipo_B_BNE),
    .out6(ImmSel[2]), .out7(Tipo_U_LUI), .sel(opcode));  // open: out8, out9, out10, out11, out12, out13, out14, out15, en
  or or_1 (ImmSel[0], MenWrite, is_U);
  or or_2 (is_U, Tipo_U_LUI, 1'b0);
  Multiplexer #(.select(2), .width(3)) multiplexer_1 (
    .in0(3'b000), .in1(Funct3), .in2(3'b001), .in3(3'b001), .out(ALUOp), .sel({ImmSel[1], ALUOpSel[0]}));
  // Probe on ImmSel
  // Probe on {ImmSel[1], ALUOpSel[0]}
  or or_3 (ImmSel[1], Tipo_B, Tipo_B_BNE);
  // Probe on ALUSrc
  or or_4 (ALUSrc, is_I, MenWrite);
  or or_5 (is_I, MenToReg, Tipo_I_AR, 1'b0);
  or or_6 (RegWrite, ALUOpSel[0], is_I, is_U);
  // Probe on RegWrite
  xor xor_1 (branch_cond, ALUzero, Tipo_B_BNE);
  and and_1 (branch_taken, ImmSel[1], branch_cond);
  or or_7 (PCSrc, branch_taken, ImmSel[2]);
  or or_8 (MenRead, MenToReg, Tipo_U_LUI);
  // Probe on ALUOp
  // Probe on RegWrite

  assign Tipo_B_GERAL = ImmSel[1];

  // Other names for the same wires on the sheet: Tipo_R = ALUOpSel[0]; ALUOpSel[1] = ImmSel[1]; Tipo_J = ImmSel[2];
  //   Tipo_I_Load = MenToReg; Tipo_S = MenWrite

  // Notes on the sheet:
  //   tipo U
  //   beq ou bne
  //   0000 tipo_R
  //   0001 Tipo_I_ADDI
  //   0010 Tipo_I_Load
  //   0011 Tipo_S
  //   0101 Tipo_B
  //   0110 Tipo_J
  //   ALUSrc
  //   RegWrite
endmodule
